// Digital circuit ALU.dig as structural Verilog
module ALU (
  input  [31:0] A,
  input  [31:0] B,
  input  [3:0] op,
  output [31:0] ALU_res
);

  wire [0:0] slt, sltu;
  wire [31:0] add, \and , div, \nand , \nor , notconnected_1_out, notconnected_2_out, notconnected_3_out,
       notconnected_4_out, notconnected_5_out, \or , sub, \xnor , \xor ;
  wire [63:0] mul;

  Add #(.Bits(32)) add_1 (.a(32'hf), .b(32'hf), .c_i(1'b0), .s(add));  // open: c_o
  Sub #(.Bits(32)) sub_1 (.a(32'hf), .b(32'hf), .c_i(1'b0), .s(sub));  // open: c_o
  Mul #(.Bits(32)) mul_1 (.a(32'hf), .b(32'hf), .mul(mul));
  Div #(.Bits(32)) div_1 (.a(32'hf), .b(32'hf), .q(div));  // open: r
  assign \and  = 32'hf & 32'hf;  // And and_1, 32 bits wide
  assign \or  = 32'hf | 32'hf;  // Or or_1, 32 bits wide
  assign \xor  = 32'hf ^ 32'hf;  // XOr xor_1, 32 bits wide
  assign \nor  = ~(32'hf | 32'hf);  // NOr nor_1, 32 bits wide
  assign \nand  = ~(32'hf & 32'hf);  // NAnd nand_1, 32 bits wide
  assign \xnor  = ~(32'hf ^ 32'hf);  // XNOr xnor_1, 32 bits wide
  Comparator #(.Bits(32)) u_SLT (.a(32'hf), .b(32'hf), .gt(slt[0]));  // open: eq, lt
  Comparator #(.Signed("true"), .Bits(32)) u_SLTU (.a(32'hf), .b(32'hf), .gt(sltu[0]));  // open: eq, lt
  Multiplexer #(.Selector_Bits(4), .Bits(32)) multiplexer_1 (
    .sel(4'b0111), .in_0(add), .in_1(sub), .in_2(div), .in_3(\and ), .in_4(\or ), .in_5(\xor ), .in_6(\nor ),
    .in_7(\nand ), .in_8(\xnor ), .in_9({{31{1'b0}}, slt[0]}), .in_10({{31{1'b0}}, sltu[0]}),
    .in_11(notconnected_1_out), .in_12(notconnected_2_out), .in_13(notconnected_3_out),
    .in_14(notconnected_4_out), .in_15(notconnected_5_out), .out(ALU_res));
  // NotConnected on notconnected_1_out
  // NotConnected on notconnected_2_out
  // NotConnected on notconnected_3_out
  // NotConnected on notconnected_4_out
  // NotConnected on notconnected_5_out
endmodule
