// Digital circuit Program Counter + Program Memory.dig as structural Verilog
module Program_Counter___Program_Memory (
  input  nextpc,
  input  clk
);

  wire alu_1_p4, alubsrc, alures, imm_gen_1_imm, multiplexer_1_out, register_unit_1_p7, rs1d;
  wire [2:0] f3;
  wire [4:0] rd, rs1, rs2;
  wire [6:0] f7, opc;
  wire [23:0] PC_q;

  Register PC (.D(nextpc), .C(clk), .en(1'b1), .Q(PC_q[0]));
  // control_unit control_unit_1: pin names not known; wires that end beside it: opc, alubsrc
  ROM #(.AddrBits(24), .Bits(32)) ProgramMem (.A(PC_q), .sel(1'b1), .D({f7, rs2, rs1, f3, rd, opc}));
  // Probe on {f7, rs2, rs1, f3, rd, opc}
  // Register_Unit register_unit_1: pin names not known; wires that end beside it: clk, rs1, rs2, rd, alures, rs1d, register_unit_1_p7
  imm_gen imm_gen_1 (.rs2(rs2), .f7(f7), .imm(imm_gen_1_imm));
  Multiplexer multiplexer_1 (.sel(alubsrc), .in_0(register_unit_1_p7), .in_1(imm_gen_1_imm), .out(multiplexer_1_out));
  // ALU alu_1: pin names not known; wires that end beside it: rs1d, multiplexer_1_out, 1'b0, alu_1_p4
  // data_memory data_memory_1: pin names not known; wires that end beside it: alu_1_p4, clk
  // Pins of 1 and 24 bits meet at PC_q
endmodule
