// Digital circuit Register Unit.dig as structural Verilog
module Register_Unit (
  input  clk,
  input  [4:0] rs1,
  input  [4:0] rs2,
  input  [4:0] rd,
  input  [31:0] data,
  output [31:0] rs1_data,
  output [31:0] rs2_data
);

  wire en0, en1, en2, en3, en4, en5, en6, en7, en8, en9, en10, en11, en12, en13, en14, en15, en16, en17,
       en18, en19, en20, en21, en22, en23, en24, en25, en26, en27, en28, en29, en30, en31;
  wire [31:0] x0, x1, x2, x3, x4, x5, x6, x7, x8, x9, x10, x11, x12, x13, x14, x15, x16, x17, x18, x19, x20,
       x21, x22, x23, x24, x25, x26, x27, x28, x29, x30, x31;

  Demultiplexer #(.Selector_Bits(5)) demultiplexer_1 (
    .sel(rd), .in(1'b0), .out_0(en0), .out_1(en1), .out_2(en2), .out_3(en3), .out_4(en4), .out_5(en5),
    .out_6(en6), .out_7(en7), .out_8(en8), .out_9(en9), .out_10(en10), .out_11(en11), .out_12(en12),
    .out_13(en13), .out_14(en14), .out_15(en15), .out_16(en16), .out_17(en17), .out_18(en18), .out_19(en19),
    .out_20(en20), .out_21(en21), .out_22(en22), .out_23(en23), .out_24(en24), .out_25(en25), .out_26(en26),
    .out_27(en27), .out_28(en28), .out_29(en29), .out_30(en30), .out_31(en31));
  Register #(.Bits(32)) u_x0 (.D({32{1'b0}}), .C(clk), .en(en0), .Q(x0));
  Register #(.Bits(32)) u_x1 (.D(data), .C(clk), .en(en1), .Q(x1));
  Register #(.Bits(32)) u_x2 (.D(data), .C(clk), .en(en2), .Q(x2));
  Register #(.Bits(32)) u_x3 (.D(data), .C(clk), .en(en3), .Q(x3));
  Register #(.Bits(32)) u_x4 (.D(data), .C(clk), .en(en4), .Q(x4));
  Register #(.Bits(32)) u_x5 (.D(data), .C(clk), .en(en5), .Q(x5));
  Register #(.Bits(32)) u_x6 (.D(data), .C(clk), .en(en6), .Q(x6));
  Register #(.Bits(32)) u_x7 (.D(data), .C(clk), .en(en7), .Q(x7));
  Register #(.Bits(32)) u_x8 (.D(data), .C(clk), .en(en8), .Q(x8));
  Register #(.Bits(32)) u_x9 (.D(data), .C(clk), .en(en9), .Q(x9));
  Register #(.Bits(32)) u_x10 (.D(data), .C(clk), .en(en10), .Q(x10));
  Register #(.Bits(32)) u_x11 (.D(data), .C(clk), .en(en11), .Q(x11));
  Register #(.Bits(32)) u_x12 (.D(data), .C(clk), .en(en12), .Q(x12));
  Register #(.Bits(32)) u_x13 (.D(data), .C(clk), .en(en13), .Q(x13));
  Register #(.Bits(32)) u_x14 (.D(data), .C(clk), .en(en14), .Q(x14));
  Register #(.Bits(32)) u_x15 (.D(data), .C(clk), .en(en15), .Q(x15));
  Register #(.Bits(32)) u_x16 (.D(data), .C(clk), .en(en16), .Q(x16));
  Register #(.Bits(32)) u_x17 (.D(data), .C(clk), .en(en17), .Q(x17));
  Register #(.Bits(32)) u_x18 (.D(data), .C(clk), .en(en18), .Q(x18));
  Register #(.Bits(32)) u_x19 (.D(data), .C(clk), .en(en19), .Q(x19));
  Register #(.Bits(32)) u_x20 (.D(data), .C(clk), .en(en20), .Q(x20));
  Register #(.Bits(32)) u_x21 (.D(data), .C(clk), .en(en21), .Q(x21));
  Register #(.Bits(32)) u_x22 (.D(data), .C(clk), .en(en22), .Q(x22));
  Register #(.Bits(32)) u_x23 (.D(data), .C(clk), .en(en23), .Q(x23));
  Register #(.Bits(32)) u_x24 (.D(data), .C(clk), .en(en24), .Q(x24));
  Register #(.Bits(32)) u_x25 (.D(data), .C(clk), .en(en25), .Q(x25));
  Register #(.Bits(32)) u_x26 (.D(data), .C(clk), .en(en26), .Q(x26));
  Register #(.Bits(32)) u_x27 (.D(data), .C(clk), .en(en27), .Q(x27));
  Register #(.Bits(32)) u_x28 (.D(data), .C(clk), .en(en28), .Q(x28));
  Register #(.Bits(32)) u_x29 (.D(data), .C(clk), .en(en29), .Q(x29));
  Register #(.Bits(32)) u_x30 (.D(data), .C(clk), .en(en30), .Q(x30));
  Register #(.Bits(32)) u_x31 (.D(data), .C(clk), .en(en31), .Q(x31));
  Multiplexer #(.Selector_Bits(5), .Bits(32)) multiplexer_1 (
    .sel(rs1), .in_0(x0), .in_1(x1), .in_2(x2), .in_3(x3), .in_4(x4), .in_5(x5), .in_6(x6), .in_7(x7),
    .in_8(x8), .in_9(x9), .in_10(x10), .in_11(x11), .in_12(x12), .in_13(x13), .in_14(x14), .in_15(x15),
    .in_16(x16), .in_17(x17), .in_18(x18), .in_19(x19), .in_20(x20), .in_21(x21), .in_22(x22), .in_23(x23),
    .in_24(x24), .in_25(x25), .in_26(x26), .in_27(x27), .in_28(x28), .in_29(x29), .in_30(x30), .in_31(x31),
    .out(rs1_data));
  Multiplexer #(.Selector_Bits(5), .Bits(32)) multiplexer_2 (
    .sel(rs2), .in_0(x0), .in_1(x1), .in_2(x2), .in_3(x3), .in_4(x4), .in_5(x5), .in_6(x6), .in_7(x7),
    .in_8(x8), .in_9(x9), .in_10(x10), .in_11(x11), .in_12(x12), .in_13(x13), .in_14(x14), .in_15(x15),
    .in_16(x16), .in_17(x17), .in_18(x18), .in_19(x19), .in_20(x20), .in_21(x21), .in_22(x22), .in_23(x23),
    .in_24(x24), .in_25(x25), .in_26(x26), .in_27(x27), .in_28(x28), .in_29(x29), .in_30(x30), .in_31(x31),
    .out(rs2_data));
endmodule
