// Digital circuit data memory.dig as structural Verilog
module data_memory (
  input  [31:0] address,
  input  [31:0] data,
  input  we,
  input  [2:0] ctrl,
  input  [2:0] clk,
  output [31:0] out
);

  wire lb, lbu, lh, lhu;
  wire [7:0] out_0, out_1, out_2, out_3;
  wire [23:0] addr;
  wire [31:0] bitextender_1_out, bitextender_2_out, multiplexer_1_out, multiplexer_2_out, multiplexer_3_out;
  wire [31:24] div4_out;

  BarrelShifter #(.Bits(32)) div4 (.in(address), .shift(6'b000010), .out({div4_out, addr}));
  RAMDualPort #(.AddrBits(24), .Bits(8)) RAM1 (.A(addr), .Din(data[15:8]), .str(we), .C(clk[0]), .ld(1'b1), .D(out_1));
  RAMDualPort #(.AddrBits(24), .Bits(8)) RAM3 (.A(addr), .Din(data[31:24]), .str(we), .C(clk[0]), .ld(1'b1), .D(out_3));
  Comparator #(.Bits(3)) u_lb (.a(ctrl), .b(3'b000), .eq(lb));  // open: gt, lt
  Comparator #(.Bits(3)) u_lbu (.a(ctrl), .b(3'b100), .eq(lbu));  // open: gt, lt
  RAMDualPort #(.AddrBits(24), .Bits(8)) RAM0 (.A(addr), .Din(data[7:0]), .str(we), .C(clk[0]), .ld(1'b1), .D(out_0));
  RAMDualPort #(.AddrBits(24), .Bits(8)) RAM2 (.A(addr), .Din(data[23:16]), .str(we), .C(clk[0]), .ld(1'b1), .D(out_2));
  Comparator #(.Bits(3)) u_lh (.a(ctrl), .b(3'b010), .eq(lh));  // open: gt, lt
  Comparator #(.Bits(3)) u_lhu (.a(ctrl), .b(3'b110), .eq(lhu));  // open: gt, lt
  Multiplexer #(.Bits(32)) multiplexer_1 (
    .sel(lhu), .in_0({out_3, out_2, out_1, out_0}), .in_1({{16{1'b0}}, out_1, out_0}), .out(multiplexer_1_out));
  BitExtender #(.inputBits(16), .outputBits(32)) bitextender_1 (.in({out_1, out_0}), .out(bitextender_1_out));
  Multiplexer #(.Bits(32)) multiplexer_2 (
    .sel(lh), .in_0(multiplexer_1_out), .in_1(bitextender_1_out), .out(multiplexer_2_out));
  Multiplexer #(.Bits(32)) multiplexer_3 (
    .sel(lbu), .in_0(multiplexer_2_out), .in_1({{24{1'b0}}, out_0}), .out(multiplexer_3_out));
  BitExtender #(.outputBits(32)) bitextender_2 (.in(out_0), .out(bitextender_2_out));
  Multiplexer #(.Bits(32)) multiplexer_4 (.sel(lb), .in_0(multiplexer_3_out), .in_1(bitextender_2_out), .out(out));
  // Pins of 1 and 3 bits meet at clk

  // Other names for the same wires on the sheet: data_0[7:0] = data[7:0]; data_in[31:0] = data;
  //   data_1[7:0] = data[15:8]; data_2[7:0] = data[23:16]; data_3[7:0] = data[31:24]
endmodule
