// Digital circuit imm gen.dig as structural Verilog
module imm_gen (
  input  [11:0] rs2,
  input  [11:0] f7,
  output imm
);

  wire [11:0] comparator_1_eq;

  Comparator #(.Bits(12)) comparator_1 (.a(rs2), .b(f7), .eq(comparator_1_eq[0]));  // open: gt, lt
  Comparator #(.Bits(12)) comparator_2 (.a(comparator_1_eq), .b({12{1'b0}}), .eq(imm));  // open: gt, lt
  // Pins of 5 and 12 bits meet at rs2
  // Pins of 7 and 12 bits meet at f7
  // Pins of 1 and 12 bits meet at comparator_1_eq
  // Pins of 12 and 20 bits meet at {20{1'b0}}
endmodule
